# Fritzing sketch SensorLog (saved by Fritzing 0.8.3b)
breadboards: 1

parts:
  DHT1 = DHT22 Humidity and Temperature Sensor
  Part2 = Memoire 1.0 - SD card log shield
  R1 = Resistor [tolerance=±5% resistance=10k package=THT]  # not connected

nets:
  VDD: DHT1.VDD, Part2.+5V
  N1: DHT1.DATA, Part2.DIG_2
  GND: DHT1.GND, Part2.GND

notes:
  NOTE:
  The data logger used is the Adafruit data logger shield (https://www.adafruit.com/product/1141), not the one displayed here.
